// Logisim project alu.circ as structural Verilog: 15 circuits, main circuit main
module main (
  input  [31:0] X,
  input  [31:0] Y,
  input  [3:0] Switch,
  output Signed_Overflow,
  output Equal,
  output [31:0] Result
);

  wire addV, subV;
  wire [4:0] logical_x_splitter_1__5_bit_x_output, logical_x_splitter_2__5_bit_x_output,
       logical_x_splitter_3__5_bit_x_output;
  wire [31:0] add_1_result, addu_1_unsigned_result, and_1_result, or_1_result, shifter_1_out, shifter_2_out,
       shifter_3_out, slt_signed_comparison_1_set, sltu_unsigned_1_set, sub_1_result, subu_1_result;

  logical_X_splitter logical_x_splitter_1 (.X_Value(X), ._5_bit_X_Output(logical_x_splitter_1__5_bit_x_output));
  logical_X_splitter logical_x_splitter_2 (.X_Value(X), ._5_bit_X_Output(logical_x_splitter_2__5_bit_x_output));
  logical_X_splitter logical_x_splitter_3 (.X_Value(X), ._5_bit_X_Output(logical_x_splitter_3__5_bit_x_output));
  equal_check equal_check_1 (.A(X), .B(Y), .result(Equal));
  sub sub_1 (.A(X), .B(Y), .Result(sub_1_result), .Signed_Overflow(subV));
  addu addu_1 (.A(X), .B(Y), .unsigned_result(addu_1_unsigned_result));
  add add_1 (.A(X), .B(Y), .Result(add_1_result), .Signed_Overflow(addV));
  Shifter #(.width(32), .shift("ar")) shifter_1 (
    .in(Y), .\dist (logical_x_splitter_1__5_bit_x_output), .out(shifter_1_out));
  Shifter #(.width(32), .shift("lr")) shifter_2 (
    .in(Y), .\dist (logical_x_splitter_2__5_bit_x_output), .out(shifter_2_out));
  Shifter #(.width(32)) shifter_3 (.in(Y), .\dist (logical_x_splitter_3__5_bit_x_output), .out(shifter_3_out));
  Multiplexer #(.select(4), .width(32)) multiplexer_1 (
    .in0(shifter_3_out), .in1(shifter_2_out), .in2(shifter_1_out), .in5(add_1_result),
    .in6(addu_1_unsigned_result), .in7(sub_1_result), .in8(subu_1_result), .in9(and_1_result),
    .in10(or_1_result), .in14(slt_signed_comparison_1_set), .in15(sltu_unsigned_1_set), .out(Result),
    .sel(Switch));  // open: in3, in4, in11, in12, in13, en
  Multiplexer #(.select(4)) multiplexer_2 (
    .in0(1'b0), .in1(1'b0), .in2(1'b0), .in5(addV), .in6(1'b0), .in7(subV), .in8(1'b0), .in9(1'b0),
    .in10(1'b0), .in14(1'b0), .in15(1'b0), .out(Signed_Overflow), .sel(Switch));  // open: in3, in4, in11, in12, in13, en
  subu subu_1 (.A(X), .B(Y), .Result(subu_1_result));
  \and  and_1 (.A(X), .B(Y), .Result(and_1_result));
  \or  or_1 (.A(X), .B(Y), .Result(or_1_result));
  slt_signed_comparison slt_signed_comparison_1 (.A(X), .B(Y), .Set(slt_signed_comparison_1_set));
  sltu_unsigned sltu_unsigned_1 (.A(X), .B(Y), .Set(sltu_unsigned_1_set));

  // Other names for the same wires on the sheet: overflow = Signed_Overflow; S[3:0] = Switch

  // Notes on the sheet:
  //   INPUTS to your circuit
  //   DON'T CHANGE THE LOCATIONS OF THE INPUTS AND OUTPUTS!
  //   OUTPUTS from your circuit
endmodule

module logical_X_splitter (
  input  [31:0] X_Value,
  output [4:0] _5_bit_X_Output
);


  assign _5_bit_X_Output = X_Value[4:0];

  // Notes on the sheet:
  //   The splitter here takes only the 5 right most bits (Least Significant Bits) and converts this 32 bit X value into a 5-bit Value using another splitter.
  //   The reason to do this is because the bit shifters accept only 5-bit values (Integers 0-32) to shift the bits in Y value, which has only 32-bits   
endmodule

module overflow_for_add (
  input  Most_Significant_A_Bit,
  input  Last_Result_Bit,
  input  Most_Significant_B_Bit,
  output Signed_Overflow
);

  wire and_1_out, and_2_out, not_1_out, not_2_out, not_3_out;

  not not_1 (not_1_out, Most_Significant_A_Bit);
  not not_2 (not_2_out, Most_Significant_B_Bit);
  not not_3 (not_3_out, Last_Result_Bit);
  and and_1 (and_1_out, not_1_out, Last_Result_Bit, not_2_out);
  and and_2 (and_2_out, Most_Significant_A_Bit, not_3_out, Most_Significant_B_Bit);
  or or_1 (Signed_Overflow, and_1_out, and_2_out);

  // Notes on the sheet:
  //   Boolean representation: (~A * ~B * C) + (A * B * ~C)
  //   Overflow occurs in "add" only if the most-significant bit (31) is the same for both X and Y inputs but the result bit (31) of them both is the opposite. 
endmodule

module add (
  input  [31:0] A,
  input  [31:0] B,
  output [31:0] Result,
  output Signed_Overflow
);

  wire adder_1_cout, adder_2_cout, adder_3_cout, adder_4_cout, adder_5_cout, adder_6_cout, adder_7_cout,
       adder_8_cout, adder_9_cout, adder_10_cout, adder_11_cout, adder_12_cout, adder_13_cout, adder_14_cout,
       adder_15_cout, adder_16_cout, adder_17_cout, adder_18_cout, adder_19_cout, adder_20_cout,
       adder_21_cout, adder_22_cout, adder_23_cout, adder_24_cout, adder_25_cout, adder_26_cout,
       adder_27_cout, adder_28_cout, adder_29_cout, adder_30_cout, adder_31_cout;

  Adder #(.width(1)) adder_1 (.a(A[0]), .b(B[0]), .out(Result[0]), .cin(1'b0), .cout(adder_1_cout));
  Adder #(.width(1)) adder_2 (.a(A[1]), .b(B[1]), .out(Result[1]), .cin(adder_1_cout), .cout(adder_2_cout));
  Adder #(.width(1)) adder_3 (.a(A[2]), .b(B[2]), .out(Result[2]), .cin(adder_2_cout), .cout(adder_3_cout));
  Adder #(.width(1)) adder_4 (.a(A[3]), .b(B[3]), .out(Result[3]), .cin(adder_3_cout), .cout(adder_4_cout));
  Adder #(.width(1)) adder_5 (.a(A[4]), .b(B[4]), .out(Result[4]), .cin(adder_4_cout), .cout(adder_5_cout));
  Adder #(.width(1)) adder_6 (.a(A[5]), .b(B[5]), .out(Result[5]), .cin(adder_5_cout), .cout(adder_6_cout));
  Adder #(.width(1)) adder_7 (.a(A[6]), .b(B[6]), .out(Result[6]), .cin(adder_6_cout), .cout(adder_7_cout));
  Adder #(.width(1)) adder_8 (.a(A[7]), .b(B[7]), .out(Result[7]), .cin(adder_7_cout), .cout(adder_8_cout));
  Adder #(.width(1)) adder_9 (.a(A[8]), .b(B[8]), .out(Result[8]), .cin(adder_8_cout), .cout(adder_9_cout));
  Adder #(.width(1)) adder_10 (.a(A[9]), .b(B[9]), .out(Result[9]), .cin(adder_9_cout), .cout(adder_10_cout));
  Adder #(.width(1)) adder_11 (.a(A[10]), .b(B[10]), .out(Result[10]), .cin(adder_10_cout), .cout(adder_11_cout));
  Adder #(.width(1)) adder_12 (.a(A[11]), .b(B[11]), .out(Result[11]), .cin(adder_11_cout), .cout(adder_12_cout));
  Adder #(.width(1)) adder_13 (.a(A[12]), .b(B[12]), .out(Result[12]), .cin(adder_12_cout), .cout(adder_13_cout));
  Adder #(.width(1)) adder_14 (.a(A[13]), .b(B[13]), .out(Result[13]), .cin(adder_13_cout), .cout(adder_14_cout));
  Adder #(.width(1)) adder_15 (.a(A[14]), .b(B[14]), .out(Result[14]), .cin(adder_14_cout), .cout(adder_15_cout));
  Adder #(.width(1)) adder_16 (.a(A[15]), .b(B[15]), .out(Result[15]), .cin(adder_15_cout), .cout(adder_16_cout));
  Adder #(.width(1)) adder_17 (.a(A[16]), .b(B[16]), .out(Result[16]), .cin(adder_16_cout), .cout(adder_17_cout));
  Adder #(.width(1)) adder_18 (.a(A[17]), .b(B[17]), .out(Result[17]), .cin(adder_17_cout), .cout(adder_18_cout));
  Adder #(.width(1)) adder_19 (.a(A[18]), .b(B[18]), .out(Result[18]), .cin(adder_18_cout), .cout(adder_19_cout));
  Adder #(.width(1)) adder_20 (.a(A[19]), .b(B[19]), .out(Result[19]), .cin(adder_19_cout), .cout(adder_20_cout));
  Adder #(.width(1)) adder_21 (.a(A[20]), .b(B[20]), .out(Result[20]), .cin(adder_20_cout), .cout(adder_21_cout));
  Adder #(.width(1)) adder_22 (.a(A[21]), .b(B[21]), .out(Result[21]), .cin(adder_21_cout), .cout(adder_22_cout));
  Adder #(.width(1)) adder_23 (.a(A[22]), .b(B[22]), .out(Result[22]), .cin(adder_22_cout), .cout(adder_23_cout));
  Adder #(.width(1)) adder_24 (.a(A[23]), .b(B[23]), .out(Result[23]), .cin(adder_23_cout), .cout(adder_24_cout));
  Adder #(.width(1)) adder_25 (.a(A[24]), .b(B[24]), .out(Result[24]), .cin(adder_24_cout), .cout(adder_25_cout));
  Adder #(.width(1)) adder_26 (.a(A[25]), .b(B[25]), .out(Result[25]), .cin(adder_25_cout), .cout(adder_26_cout));
  Adder #(.width(1)) adder_27 (.a(A[26]), .b(B[26]), .out(Result[26]), .cin(adder_26_cout), .cout(adder_27_cout));
  Adder #(.width(1)) adder_28 (.a(A[27]), .b(B[27]), .out(Result[27]), .cin(adder_27_cout), .cout(adder_28_cout));
  Adder #(.width(1)) adder_29 (.a(A[28]), .b(B[28]), .out(Result[28]), .cin(adder_28_cout), .cout(adder_29_cout));
  Adder #(.width(1)) adder_30 (.a(A[29]), .b(B[29]), .out(Result[29]), .cin(adder_29_cout), .cout(adder_30_cout));
  Adder #(.width(1)) adder_31 (.a(A[30]), .b(B[30]), .out(Result[30]), .cin(adder_30_cout), .cout(adder_31_cout));
  Adder #(.width(1)) adder_32 (.a(A[31]), .b(B[31]), .out(Result[31]), .cin(adder_31_cout));  // open: cout
  overflow_for_add overflow_for_add_1 (
    .Most_Significant_A_Bit(A[31]), .Last_Result_Bit(Result[31]), .Most_Significant_B_Bit(B[31]),
    .Signed_Overflow(Signed_Overflow));
endmodule

module addu (
  input  [31:0] A,
  input  [31:0] B,
  output [31:0] unsigned_result
);

  wire adder_1_cout, adder_2_cout, adder_3_cout, adder_4_cout, adder_5_cout, adder_6_cout, adder_7_cout,
       adder_8_cout, adder_9_cout, adder_10_cout, adder_11_cout, adder_12_cout, adder_13_cout, adder_14_cout,
       adder_15_cout, adder_16_cout, adder_17_cout, adder_18_cout, adder_19_cout, adder_20_cout,
       adder_21_cout, adder_22_cout, adder_23_cout, adder_24_cout, adder_25_cout, adder_26_cout,
       adder_27_cout, adder_28_cout, adder_29_cout, adder_30_cout, adder_31_cout;

  Adder #(.width(1)) adder_1 (.a(A[0]), .b(B[0]), .out(unsigned_result[0]), .cin(1'b0), .cout(adder_1_cout));
  Adder #(.width(1)) adder_2 (.a(A[1]), .b(B[1]), .out(unsigned_result[1]), .cin(adder_1_cout), .cout(adder_2_cout));
  Adder #(.width(1)) adder_3 (.a(A[2]), .b(B[2]), .out(unsigned_result[2]), .cin(adder_2_cout), .cout(adder_3_cout));
  Adder #(.width(1)) adder_4 (.a(A[3]), .b(B[3]), .out(unsigned_result[3]), .cin(adder_3_cout), .cout(adder_4_cout));
  Adder #(.width(1)) adder_5 (.a(A[4]), .b(B[4]), .out(unsigned_result[4]), .cin(adder_4_cout), .cout(adder_5_cout));
  Adder #(.width(1)) adder_6 (.a(A[5]), .b(B[5]), .out(unsigned_result[5]), .cin(adder_5_cout), .cout(adder_6_cout));
  Adder #(.width(1)) adder_7 (.a(A[6]), .b(B[6]), .out(unsigned_result[6]), .cin(adder_6_cout), .cout(adder_7_cout));
  Adder #(.width(1)) adder_8 (.a(A[7]), .b(B[7]), .out(unsigned_result[7]), .cin(adder_7_cout), .cout(adder_8_cout));
  Adder #(.width(1)) adder_9 (.a(A[8]), .b(B[8]), .out(unsigned_result[8]), .cin(adder_8_cout), .cout(adder_9_cout));
  Adder #(.width(1)) adder_10 (.a(A[9]), .b(B[9]), .out(unsigned_result[9]), .cin(adder_9_cout), .cout(adder_10_cout));
  Adder #(.width(1)) adder_11 (
    .a(A[10]), .b(B[10]), .out(unsigned_result[10]), .cin(adder_10_cout), .cout(adder_11_cout));
  Adder #(.width(1)) adder_12 (
    .a(A[11]), .b(B[11]), .out(unsigned_result[11]), .cin(adder_11_cout), .cout(adder_12_cout));
  Adder #(.width(1)) adder_13 (
    .a(A[12]), .b(B[12]), .out(unsigned_result[12]), .cin(adder_12_cout), .cout(adder_13_cout));
  Adder #(.width(1)) adder_14 (
    .a(A[13]), .b(B[13]), .out(unsigned_result[13]), .cin(adder_13_cout), .cout(adder_14_cout));
  Adder #(.width(1)) adder_15 (
    .a(A[14]), .b(B[14]), .out(unsigned_result[14]), .cin(adder_14_cout), .cout(adder_15_cout));
  Adder #(.width(1)) adder_16 (
    .a(A[15]), .b(B[15]), .out(unsigned_result[15]), .cin(adder_15_cout), .cout(adder_16_cout));
  Adder #(.width(1)) adder_17 (
    .a(A[16]), .b(B[16]), .out(unsigned_result[16]), .cin(adder_16_cout), .cout(adder_17_cout));
  Adder #(.width(1)) adder_18 (
    .a(A[17]), .b(B[17]), .out(unsigned_result[17]), .cin(adder_17_cout), .cout(adder_18_cout));
  Adder #(.width(1)) adder_19 (
    .a(A[18]), .b(B[18]), .out(unsigned_result[18]), .cin(adder_18_cout), .cout(adder_19_cout));
  Adder #(.width(1)) adder_20 (
    .a(A[19]), .b(B[19]), .out(unsigned_result[19]), .cin(adder_19_cout), .cout(adder_20_cout));
  Adder #(.width(1)) adder_21 (
    .a(A[20]), .b(B[20]), .out(unsigned_result[20]), .cin(adder_20_cout), .cout(adder_21_cout));
  Adder #(.width(1)) adder_22 (
    .a(A[21]), .b(B[21]), .out(unsigned_result[21]), .cin(adder_21_cout), .cout(adder_22_cout));
  Adder #(.width(1)) adder_23 (
    .a(A[22]), .b(B[22]), .out(unsigned_result[22]), .cin(adder_22_cout), .cout(adder_23_cout));
  Adder #(.width(1)) adder_24 (
    .a(A[23]), .b(B[23]), .out(unsigned_result[23]), .cin(adder_23_cout), .cout(adder_24_cout));
  Adder #(.width(1)) adder_25 (
    .a(A[24]), .b(B[24]), .out(unsigned_result[24]), .cin(adder_24_cout), .cout(adder_25_cout));
  Adder #(.width(1)) adder_26 (
    .a(A[25]), .b(B[25]), .out(unsigned_result[25]), .cin(adder_25_cout), .cout(adder_26_cout));
  Adder #(.width(1)) adder_27 (
    .a(A[26]), .b(B[26]), .out(unsigned_result[26]), .cin(adder_26_cout), .cout(adder_27_cout));
  Adder #(.width(1)) adder_28 (
    .a(A[27]), .b(B[27]), .out(unsigned_result[27]), .cin(adder_27_cout), .cout(adder_28_cout));
  Adder #(.width(1)) adder_29 (
    .a(A[28]), .b(B[28]), .out(unsigned_result[28]), .cin(adder_28_cout), .cout(adder_29_cout));
  Adder #(.width(1)) adder_30 (
    .a(A[29]), .b(B[29]), .out(unsigned_result[29]), .cin(adder_29_cout), .cout(adder_30_cout));
  Adder #(.width(1)) adder_31 (
    .a(A[30]), .b(B[30]), .out(unsigned_result[30]), .cin(adder_30_cout), .cout(adder_31_cout));
  Adder #(.width(1)) adder_32 (.a(A[31]), .b(B[31]), .out(unsigned_result[31]), .cin(adder_31_cout));  // open: cout
endmodule

module overflow_for_sub (
  input  Most_Significant_A_Bit,
  input  Last_Result_Bit,
  input  Most_Significant_B_Bit,
  output out
);

  wire and_1_out, and_2_out, not_1_out, not_2_out, not_3_out;

  not not_1 (not_1_out, Last_Result_Bit);
  not not_2 (not_2_out, Most_Significant_B_Bit);
  not not_3 (not_3_out, Most_Significant_A_Bit);
  and and_1 (and_1_out, Most_Significant_A_Bit, not_1_out, not_2_out);
  and and_2 (and_2_out, not_3_out, Last_Result_Bit, Most_Significant_B_Bit);
  or or_1 (out, and_1_out, and_2_out);
endmodule

module sub (
  input  [31:0] A,
  input  [31:0] B,
  output [31:0] Result,
  output Signed_Overflow
);

  wire adder_1_cout, adder_2_cout, adder_3_cout, adder_4_cout, adder_5_cout, adder_6_cout, adder_7_cout,
       adder_8_cout, adder_9_cout, adder_10_cout, adder_11_cout, adder_12_cout, adder_13_cout, adder_14_cout,
       adder_15_cout, adder_16_cout, adder_17_cout, adder_18_cout, adder_19_cout, adder_20_cout,
       adder_21_cout, adder_22_cout, adder_23_cout, adder_24_cout, adder_25_cout, adder_26_cout,
       adder_27_cout, adder_28_cout, adder_29_cout, adder_30_cout, adder_31_cout, B0, B1, B2, B3, B4, B5, B6,
       B7, B8, B9, B10, B11, B12, B13, B14, B15, B16, B17, B18, B19, B20, B21, B22, B23, B24, B25, B26, B27,
       B28, B29, B30, B31;

  not not_1 (B0, B[0]);
  not not_2 (B1, B[1]);
  not not_3 (B2, B[2]);
  not not_4 (B3, B[3]);
  not not_5 (B4, B[4]);
  not not_6 (B5, B[5]);
  not not_7 (B6, B[6]);
  not not_8 (B7, B[7]);
  not not_9 (B8, B[8]);
  not not_10 (B9, B[9]);
  not not_11 (B10, B[10]);
  not not_12 (B11, B[11]);
  not not_13 (B12, B[12]);
  not not_14 (B13, B[13]);
  not not_15 (B14, B[14]);
  not not_16 (B15, B[15]);
  not not_17 (B16, B[16]);
  not not_18 (B17, B[17]);
  not not_19 (B18, B[18]);
  not not_20 (B19, B[19]);
  not not_21 (B20, B[20]);
  not not_22 (B21, B[21]);
  not not_23 (B22, B[22]);
  not not_24 (B23, B[23]);
  not not_25 (B24, B[24]);
  not not_26 (B25, B[25]);
  not not_27 (B26, B[26]);
  not not_28 (B27, B[27]);
  not not_29 (B28, B[28]);
  not not_30 (B29, B[29]);
  not not_31 (B30, B[30]);
  not not_32 (B31, B[31]);
  Adder #(.width(1)) adder_1 (.a(A[0]), .b(B0), .out(Result[0]), .cin(1'b1), .cout(adder_1_cout));
  Adder #(.width(1)) adder_2 (.a(A[1]), .b(B1), .out(Result[1]), .cin(adder_1_cout), .cout(adder_2_cout));
  Adder #(.width(1)) adder_3 (.a(A[2]), .b(B2), .out(Result[2]), .cin(adder_2_cout), .cout(adder_3_cout));
  Adder #(.width(1)) adder_4 (.a(A[3]), .b(B3), .out(Result[3]), .cin(adder_3_cout), .cout(adder_4_cout));
  Adder #(.width(1)) adder_5 (.a(A[4]), .b(B4), .out(Result[4]), .cin(adder_4_cout), .cout(adder_5_cout));
  Adder #(.width(1)) adder_6 (.a(A[5]), .b(B5), .out(Result[5]), .cin(adder_5_cout), .cout(adder_6_cout));
  Adder #(.width(1)) adder_7 (.a(A[6]), .b(B6), .out(Result[6]), .cin(adder_6_cout), .cout(adder_7_cout));
  Adder #(.width(1)) adder_8 (.a(A[7]), .b(B7), .out(Result[7]), .cin(adder_7_cout), .cout(adder_8_cout));
  Adder #(.width(1)) adder_9 (.a(A[8]), .b(B8), .out(Result[8]), .cin(adder_8_cout), .cout(adder_9_cout));
  Adder #(.width(1)) adder_10 (.a(A[9]), .b(B9), .out(Result[9]), .cin(adder_9_cout), .cout(adder_10_cout));
  Adder #(.width(1)) adder_11 (.a(A[10]), .b(B10), .out(Result[10]), .cin(adder_10_cout), .cout(adder_11_cout));
  Adder #(.width(1)) adder_12 (.a(A[11]), .b(B11), .out(Result[11]), .cin(adder_11_cout), .cout(adder_12_cout));
  Adder #(.width(1)) adder_13 (.a(A[12]), .b(B12), .out(Result[12]), .cin(adder_12_cout), .cout(adder_13_cout));
  Adder #(.width(1)) adder_14 (.a(A[13]), .b(B13), .out(Result[13]), .cin(adder_13_cout), .cout(adder_14_cout));
  Adder #(.width(1)) adder_15 (.a(A[14]), .b(B14), .out(Result[14]), .cin(adder_14_cout), .cout(adder_15_cout));
  Adder #(.width(1)) adder_16 (.a(A[15]), .b(B15), .out(Result[15]), .cin(adder_15_cout), .cout(adder_16_cout));
  Adder #(.width(1)) adder_17 (.a(A[16]), .b(B16), .out(Result[16]), .cin(adder_16_cout), .cout(adder_17_cout));
  Adder #(.width(1)) adder_18 (.a(A[17]), .b(B17), .out(Result[17]), .cin(adder_17_cout), .cout(adder_18_cout));
  Adder #(.width(1)) adder_19 (.a(A[18]), .b(B18), .out(Result[18]), .cin(adder_18_cout), .cout(adder_19_cout));
  Adder #(.width(1)) adder_20 (.a(A[19]), .b(B19), .out(Result[19]), .cin(adder_19_cout), .cout(adder_20_cout));
  Adder #(.width(1)) adder_21 (.a(A[20]), .b(B20), .out(Result[20]), .cin(adder_20_cout), .cout(adder_21_cout));
  Adder #(.width(1)) adder_22 (.a(A[21]), .b(B21), .out(Result[21]), .cin(adder_21_cout), .cout(adder_22_cout));
  Adder #(.width(1)) adder_23 (.a(A[22]), .b(B22), .out(Result[22]), .cin(adder_22_cout), .cout(adder_23_cout));
  Adder #(.width(1)) adder_24 (.a(A[23]), .b(B23), .out(Result[23]), .cin(adder_23_cout), .cout(adder_24_cout));
  Adder #(.width(1)) adder_25 (.a(A[24]), .b(B24), .out(Result[24]), .cin(adder_24_cout), .cout(adder_25_cout));
  Adder #(.width(1)) adder_26 (.a(A[25]), .b(B25), .out(Result[25]), .cin(adder_25_cout), .cout(adder_26_cout));
  Adder #(.width(1)) adder_27 (.a(A[26]), .b(B26), .out(Result[26]), .cin(adder_26_cout), .cout(adder_27_cout));
  Adder #(.width(1)) adder_28 (.a(A[27]), .b(B27), .out(Result[27]), .cin(adder_27_cout), .cout(adder_28_cout));
  Adder #(.width(1)) adder_29 (.a(A[28]), .b(B28), .out(Result[28]), .cin(adder_28_cout), .cout(adder_29_cout));
  Adder #(.width(1)) adder_30 (.a(A[29]), .b(B29), .out(Result[29]), .cin(adder_29_cout), .cout(adder_30_cout));
  Adder #(.width(1)) adder_31 (.a(A[30]), .b(B30), .out(Result[30]), .cin(adder_30_cout), .cout(adder_31_cout));
  Adder #(.width(1)) adder_32 (.a(A[31]), .b(B31), .out(Result[31]), .cin(adder_31_cout));  // open: cout
  overflow_for_sub overflow_for_sub_1 (
    .Most_Significant_A_Bit(A[31]), .Last_Result_Bit(Result[31]), .Most_Significant_B_Bit(B31),
    .out(Signed_Overflow));
endmodule

module subu (
  input  [31:0] A,
  input  [31:0] B,
  output [31:0] Result
);

  wire adder_1_cout, adder_2_cout, adder_3_cout, adder_4_cout, adder_5_cout, adder_6_cout, adder_7_cout,
       adder_8_cout, adder_9_cout, adder_10_cout, adder_11_cout, adder_12_cout, adder_13_cout, adder_14_cout,
       adder_15_cout, adder_16_cout, adder_17_cout, adder_18_cout, adder_19_cout, adder_20_cout,
       adder_21_cout, adder_22_cout, adder_23_cout, adder_24_cout, adder_25_cout, adder_26_cout,
       adder_27_cout, adder_28_cout, adder_29_cout, adder_30_cout, adder_31_cout, B0, B1, B2, B3, B4, B5, B6,
       B7, B8, B9, B10, B11, B12, B13, B14, B15, B16, B17, B18, B19, B20, B21, B22, B23, B24, B25, B26, B27,
       B28, B29, B30, B31;

  not not_1 (B0, B[0]);
  not not_2 (B1, B[1]);
  not not_3 (B2, B[2]);
  not not_4 (B3, B[3]);
  not not_5 (B4, B[4]);
  not not_6 (B5, B[5]);
  not not_7 (B6, B[6]);
  not not_8 (B7, B[7]);
  not not_9 (B8, B[8]);
  not not_10 (B9, B[9]);
  not not_11 (B10, B[10]);
  not not_12 (B11, B[11]);
  not not_13 (B12, B[12]);
  not not_14 (B13, B[13]);
  not not_15 (B14, B[14]);
  not not_16 (B15, B[15]);
  not not_17 (B16, B[16]);
  not not_18 (B17, B[17]);
  not not_19 (B18, B[18]);
  not not_20 (B19, B[19]);
  not not_21 (B20, B[20]);
  not not_22 (B21, B[21]);
  not not_23 (B22, B[22]);
  not not_24 (B23, B[23]);
  not not_25 (B24, B[24]);
  not not_26 (B25, B[25]);
  not not_27 (B26, B[26]);
  not not_28 (B27, B[27]);
  not not_29 (B28, B[28]);
  not not_30 (B29, B[29]);
  not not_31 (B30, B[30]);
  not not_32 (B31, B[31]);
  Adder #(.width(1)) adder_1 (.a(A[0]), .b(B0), .out(Result[0]), .cin(1'b1), .cout(adder_1_cout));
  Adder #(.width(1)) adder_2 (.a(A[1]), .b(B1), .out(Result[1]), .cin(adder_1_cout), .cout(adder_2_cout));
  Adder #(.width(1)) adder_3 (.a(A[2]), .b(B2), .out(Result[2]), .cin(adder_2_cout), .cout(adder_3_cout));
  Adder #(.width(1)) adder_4 (.a(A[3]), .b(B3), .out(Result[3]), .cin(adder_3_cout), .cout(adder_4_cout));
  Adder #(.width(1)) adder_5 (.a(A[4]), .b(B4), .out(Result[4]), .cin(adder_4_cout), .cout(adder_5_cout));
  Adder #(.width(1)) adder_6 (.a(A[5]), .b(B5), .out(Result[5]), .cin(adder_5_cout), .cout(adder_6_cout));
  Adder #(.width(1)) adder_7 (.a(A[6]), .b(B6), .out(Result[6]), .cin(adder_6_cout), .cout(adder_7_cout));
  Adder #(.width(1)) adder_8 (.a(A[7]), .b(B7), .out(Result[7]), .cin(adder_7_cout), .cout(adder_8_cout));
  Adder #(.width(1)) adder_9 (.a(A[8]), .b(B8), .out(Result[8]), .cin(adder_8_cout), .cout(adder_9_cout));
  Adder #(.width(1)) adder_10 (.a(A[9]), .b(B9), .out(Result[9]), .cin(adder_9_cout), .cout(adder_10_cout));
  Adder #(.width(1)) adder_11 (.a(A[10]), .b(B10), .out(Result[10]), .cin(adder_10_cout), .cout(adder_11_cout));
  Adder #(.width(1)) adder_12 (.a(A[11]), .b(B11), .out(Result[11]), .cin(adder_11_cout), .cout(adder_12_cout));
  Adder #(.width(1)) adder_13 (.a(A[12]), .b(B12), .out(Result[12]), .cin(adder_12_cout), .cout(adder_13_cout));
  Adder #(.width(1)) adder_14 (.a(A[13]), .b(B13), .out(Result[13]), .cin(adder_13_cout), .cout(adder_14_cout));
  Adder #(.width(1)) adder_15 (.a(A[14]), .b(B14), .out(Result[14]), .cin(adder_14_cout), .cout(adder_15_cout));
  Adder #(.width(1)) adder_16 (.a(A[15]), .b(B15), .out(Result[15]), .cin(adder_15_cout), .cout(adder_16_cout));
  Adder #(.width(1)) adder_17 (.a(A[16]), .b(B16), .out(Result[16]), .cin(adder_16_cout), .cout(adder_17_cout));
  Adder #(.width(1)) adder_18 (.a(A[17]), .b(B17), .out(Result[17]), .cin(adder_17_cout), .cout(adder_18_cout));
  Adder #(.width(1)) adder_19 (.a(A[18]), .b(B18), .out(Result[18]), .cin(adder_18_cout), .cout(adder_19_cout));
  Adder #(.width(1)) adder_20 (.a(A[19]), .b(B19), .out(Result[19]), .cin(adder_19_cout), .cout(adder_20_cout));
  Adder #(.width(1)) adder_21 (.a(A[20]), .b(B20), .out(Result[20]), .cin(adder_20_cout), .cout(adder_21_cout));
  Adder #(.width(1)) adder_22 (.a(A[21]), .b(B21), .out(Result[21]), .cin(adder_21_cout), .cout(adder_22_cout));
  Adder #(.width(1)) adder_23 (.a(A[22]), .b(B22), .out(Result[22]), .cin(adder_22_cout), .cout(adder_23_cout));
  Adder #(.width(1)) adder_24 (.a(A[23]), .b(B23), .out(Result[23]), .cin(adder_23_cout), .cout(adder_24_cout));
  Adder #(.width(1)) adder_25 (.a(A[24]), .b(B24), .out(Result[24]), .cin(adder_24_cout), .cout(adder_25_cout));
  Adder #(.width(1)) adder_26 (.a(A[25]), .b(B25), .out(Result[25]), .cin(adder_25_cout), .cout(adder_26_cout));
  Adder #(.width(1)) adder_27 (.a(A[26]), .b(B26), .out(Result[26]), .cin(adder_26_cout), .cout(adder_27_cout));
  Adder #(.width(1)) adder_28 (.a(A[27]), .b(B27), .out(Result[27]), .cin(adder_27_cout), .cout(adder_28_cout));
  Adder #(.width(1)) adder_29 (.a(A[28]), .b(B28), .out(Result[28]), .cin(adder_28_cout), .cout(adder_29_cout));
  Adder #(.width(1)) adder_30 (.a(A[29]), .b(B29), .out(Result[29]), .cin(adder_29_cout), .cout(adder_30_cout));
  Adder #(.width(1)) adder_31 (.a(A[30]), .b(B30), .out(Result[30]), .cin(adder_30_cout), .cout(adder_31_cout));
  Adder #(.width(1)) adder_32 (.a(A[31]), .b(B31), .out(Result[31]), .cin(adder_31_cout));  // open: cout
endmodule

module \and  (
  input  [31:0] A,
  input  [31:0] B,
  output [31:0] Result
);

  and and_1 (Result[0], A[0], B[0]);
  and and_2 (Result[1], A[1], B[1]);
  and and_3 (Result[2], A[2], B[2]);
  and and_4 (Result[3], A[3], B[3]);
  and and_5 (Result[4], A[4], B[4]);
  and and_6 (Result[5], A[5], B[5]);
  and and_7 (Result[6], A[6], B[6]);
  and and_8 (Result[7], A[7], B[7]);
  and and_9 (Result[8], A[8], B[8]);
  and and_10 (Result[9], A[9], B[9]);
  and and_11 (Result[10], A[10], B[10]);
  and and_12 (Result[11], A[11], B[11]);
  and and_13 (Result[12], A[12], B[12]);
  and and_14 (Result[13], A[13], B[13]);
  and and_15 (Result[14], A[14], B[14]);
  and and_16 (Result[15], A[15], B[15]);
  and and_17 (Result[16], A[16], B[16]);
  and and_18 (Result[17], A[17], B[17]);
  and and_19 (Result[18], A[18], B[18]);
  and and_20 (Result[19], A[19], B[19]);
  and and_21 (Result[20], A[20], B[20]);
  and and_22 (Result[21], A[21], B[21]);
  and and_23 (Result[22], A[22], B[22]);
  and and_24 (Result[23], A[23], B[23]);
  and and_25 (Result[24], A[24], B[24]);
  and and_26 (Result[25], A[25], B[25]);
  and and_27 (Result[26], A[26], B[26]);
  and and_28 (Result[27], A[27], B[27]);
  and and_29 (Result[28], A[28], B[28]);
  and and_30 (Result[29], A[29], B[29]);
  and and_31 (Result[30], A[30], B[30]);
  and and_32 (Result[31], A[31], B[31]);

  // Other names for the same wires on the sheet: R0 = Result[0]; R1 = Result[1]; R2 = Result[2]; R3 = Result[3];
  //   R4 = Result[4]; R5 = Result[5]; R6 = Result[6]; R7 = Result[7]; R8 = Result[8]; R9 = Result[9];
  //   R10 = Result[10]; R11 = Result[11]; R12 = Result[12]; R13 = Result[13]; R14 = Result[14]; R15 = Result[15];
  //   R16 = Result[16]; R17 = Result[17]; R18 = Result[18]; R19 = Result[19]; R20 = Result[20]; R21 = Result[21];
  //   R22 = Result[22]; R23 = Result[23]; R24 = Result[24]; R25 = Result[25]; R26 = Result[26]; R27 = Result[27];
  //   R28 = Result[28]; R29 = Result[29]; R30 = Result[30]; R31 = Result[31]
endmodule

module \or  (
  input  [31:0] A,
  input  [31:0] B,
  output [31:0] Result
);

  or or_1 (Result[0], A[0], B[0]);
  or or_2 (Result[1], A[1], B[1]);
  or or_3 (Result[2], A[2], B[2]);
  or or_4 (Result[3], A[3], B[3]);
  or or_5 (Result[4], A[4], B[4]);
  or or_6 (Result[5], A[5], B[5]);
  or or_7 (Result[6], A[6], B[6]);
  or or_8 (Result[7], A[7], B[7]);
  or or_9 (Result[8], A[8], B[8]);
  or or_10 (Result[9], A[9], B[9]);
  or or_11 (Result[10], A[10], B[10]);
  or or_12 (Result[11], A[11], B[11]);
  or or_13 (Result[12], A[12], B[12]);
  or or_14 (Result[13], A[13], B[13]);
  or or_15 (Result[14], A[14], B[14]);
  or or_16 (Result[15], A[15], B[15]);
  or or_17 (Result[16], A[16], B[16]);
  or or_18 (Result[17], A[17], B[17]);
  or or_19 (Result[18], A[18], B[18]);
  or or_20 (Result[19], A[19], B[19]);
  or or_21 (Result[20], A[20], B[20]);
  or or_22 (Result[21], A[21], B[21]);
  or or_23 (Result[22], A[22], B[22]);
  or or_24 (Result[23], A[23], B[23]);
  or or_25 (Result[24], A[24], B[24]);
  or or_26 (Result[25], A[25], B[25]);
  or or_27 (Result[26], A[26], B[26]);
  or or_28 (Result[27], A[27], B[27]);
  or or_29 (Result[28], A[28], B[28]);
  or or_30 (Result[29], A[29], B[29]);
  or or_31 (Result[30], A[30], B[30]);
  or or_32 (Result[31], A[31], B[31]);

  // Other names for the same wires on the sheet: R0 = Result[0]; R1 = Result[1]; R2 = Result[2]; R3 = Result[3];
  //   R4 = Result[4]; R5 = Result[5]; R6 = Result[6]; R7 = Result[7]; R8 = Result[8]; R9 = Result[9];
  //   R10 = Result[10]; R11 = Result[11]; R12 = Result[12]; R13 = Result[13]; R14 = Result[14]; R15 = Result[15];
  //   R16 = Result[16]; R17 = Result[17]; R18 = Result[18]; R19 = Result[19]; R20 = Result[20]; R21 = Result[21];
  //   R22 = Result[22]; R23 = Result[23]; R24 = Result[24]; R25 = Result[25]; R26 = Result[26]; R27 = Result[27];
  //   R28 = Result[28]; R29 = Result[29]; R30 = Result[30]; R31 = Result[31]
endmodule

module slt_signed_comparison (
  input  [31:0] A,
  input  [31:0] B,
  output [31:0] Set
);

  wire [30:0] sub_1_result;

  sub sub_1 (.A(A), .B(B), .Result({Set[0], sub_1_result}));  // open: Signed_Overflow

  assign Set[31:1] = {31{1'b0}};
endmodule

module sltu_unsigned (
  input  [31:0] A,
  input  [31:0] B,
  output [31:0] Set
);

  wire [30:0] sub_1_result;
  wire [31:0] detect_negative_1_unsigned_result, detect_negative_2_unsigned_result;

  detect_negative detect_negative_1 (.a(A), .unsigned_result(detect_negative_1_unsigned_result));
  detect_negative detect_negative_2 (.a(B), .unsigned_result(detect_negative_2_unsigned_result));
  sub sub_1 (
    .A(detect_negative_1_unsigned_result), .B(detect_negative_2_unsigned_result),
    .Result({Set[0], sub_1_result}));  // open: Signed_Overflow

  assign Set[31:1] = {31{1'b0}};
endmodule

module detect_negative (
  input  [31:0] a,
  output [31:0] unsigned_result
);

  wire [31:0] twos_complement_1__2c_result;

  twos_complement twos_complement_1 (.B(a), ._2C_result(twos_complement_1__2c_result));
  Multiplexer #(.width(32)) multiplexer_1 (
    .in0(a), .in1(twos_complement_1__2c_result), .out(unsigned_result), .sel(a[31]));  // open: en
endmodule

module twos_complement (
  input  [31:0] B,
  output [31:0] _2C_result
);

  wire adder_1_cout, adder_2_cout, adder_3_cout, adder_4_cout, adder_5_cout, adder_6_cout, adder_7_cout,
       adder_8_cout, adder_9_cout, adder_10_cout, adder_11_cout, adder_12_cout, adder_13_cout, adder_14_cout,
       adder_15_cout, adder_16_cout, adder_17_cout, adder_18_cout, adder_19_cout, adder_20_cout,
       adder_21_cout, adder_22_cout, adder_23_cout, adder_24_cout, adder_25_cout, adder_26_cout,
       adder_27_cout, adder_28_cout, adder_29_cout, adder_30_cout, adder_31_cout, B0, B1, B2, B3, B4, B5, B6,
       B7, B8, B9, B10, B11, B12, B13, B14, B15, B16, B17, B18, B19, B20, B21, B22, B23, B24, B25, B26, B27,
       B28, B29, B30, B31;

  not not_1 (B0, B[0]);
  not not_2 (B1, B[1]);
  not not_3 (B2, B[2]);
  not not_4 (B3, B[3]);
  not not_5 (B4, B[4]);
  not not_6 (B5, B[5]);
  not not_7 (B6, B[6]);
  not not_8 (B7, B[7]);
  not not_9 (B8, B[8]);
  not not_10 (B9, B[9]);
  not not_11 (B10, B[10]);
  not not_12 (B11, B[11]);
  not not_13 (B12, B[12]);
  not not_14 (B13, B[13]);
  not not_15 (B14, B[14]);
  not not_16 (B15, B[15]);
  not not_17 (B16, B[16]);
  not not_18 (B17, B[17]);
  not not_19 (B18, B[18]);
  not not_20 (B19, B[19]);
  not not_21 (B20, B[20]);
  not not_22 (B21, B[21]);
  not not_23 (B22, B[22]);
  not not_24 (B23, B[23]);
  not not_25 (B24, B[24]);
  not not_26 (B25, B[25]);
  not not_27 (B26, B[26]);
  not not_28 (B27, B[27]);
  not not_29 (B28, B[28]);
  not not_30 (B29, B[29]);
  not not_31 (B30, B[30]);
  not not_32 (B31, B[31]);
  Adder #(.width(1)) adder_1 (.a(1'b0), .b(B0), .out(_2C_result[0]), .cin(1'b1), .cout(adder_1_cout));
  Adder #(.width(1)) adder_2 (.a(1'b0), .b(B1), .out(_2C_result[1]), .cin(adder_1_cout), .cout(adder_2_cout));
  Adder #(.width(1)) adder_3 (.a(1'b0), .b(B2), .out(_2C_result[2]), .cin(adder_2_cout), .cout(adder_3_cout));
  Adder #(.width(1)) adder_4 (.a(1'b0), .b(B3), .out(_2C_result[3]), .cin(adder_3_cout), .cout(adder_4_cout));
  Adder #(.width(1)) adder_5 (.a(1'b0), .b(B4), .out(_2C_result[4]), .cin(adder_4_cout), .cout(adder_5_cout));
  Adder #(.width(1)) adder_6 (.a(1'b0), .b(B5), .out(_2C_result[5]), .cin(adder_5_cout), .cout(adder_6_cout));
  Adder #(.width(1)) adder_7 (.a(1'b0), .b(B6), .out(_2C_result[6]), .cin(adder_6_cout), .cout(adder_7_cout));
  Adder #(.width(1)) adder_8 (.a(1'b0), .b(B7), .out(_2C_result[7]), .cin(adder_7_cout), .cout(adder_8_cout));
  Adder #(.width(1)) adder_9 (.a(1'b0), .b(B8), .out(_2C_result[8]), .cin(adder_8_cout), .cout(adder_9_cout));
  Adder #(.width(1)) adder_10 (.a(1'b0), .b(B9), .out(_2C_result[9]), .cin(adder_9_cout), .cout(adder_10_cout));
  Adder #(.width(1)) adder_11 (.a(1'b0), .b(B10), .out(_2C_result[10]), .cin(adder_10_cout), .cout(adder_11_cout));
  Adder #(.width(1)) adder_12 (.a(1'b0), .b(B11), .out(_2C_result[11]), .cin(adder_11_cout), .cout(adder_12_cout));
  Adder #(.width(1)) adder_13 (.a(1'b0), .b(B12), .out(_2C_result[12]), .cin(adder_12_cout), .cout(adder_13_cout));
  Adder #(.width(1)) adder_14 (.a(1'b0), .b(B13), .out(_2C_result[13]), .cin(adder_13_cout), .cout(adder_14_cout));
  Adder #(.width(1)) adder_15 (.a(1'b0), .b(B14), .out(_2C_result[14]), .cin(adder_14_cout), .cout(adder_15_cout));
  Adder #(.width(1)) adder_16 (.a(1'b0), .b(B15), .out(_2C_result[15]), .cin(adder_15_cout), .cout(adder_16_cout));
  Adder #(.width(1)) adder_17 (.a(1'b0), .b(B16), .out(_2C_result[16]), .cin(adder_16_cout), .cout(adder_17_cout));
  Adder #(.width(1)) adder_18 (.a(1'b0), .b(B17), .out(_2C_result[17]), .cin(adder_17_cout), .cout(adder_18_cout));
  Adder #(.width(1)) adder_19 (.a(1'b0), .b(B18), .out(_2C_result[18]), .cin(adder_18_cout), .cout(adder_19_cout));
  Adder #(.width(1)) adder_20 (.a(1'b0), .b(B19), .out(_2C_result[19]), .cin(adder_19_cout), .cout(adder_20_cout));
  Adder #(.width(1)) adder_21 (.a(1'b0), .b(B20), .out(_2C_result[20]), .cin(adder_20_cout), .cout(adder_21_cout));
  Adder #(.width(1)) adder_22 (.a(1'b0), .b(B21), .out(_2C_result[21]), .cin(adder_21_cout), .cout(adder_22_cout));
  Adder #(.width(1)) adder_23 (.a(1'b0), .b(B22), .out(_2C_result[22]), .cin(adder_22_cout), .cout(adder_23_cout));
  Adder #(.width(1)) adder_24 (.a(1'b0), .b(B23), .out(_2C_result[23]), .cin(adder_23_cout), .cout(adder_24_cout));
  Adder #(.width(1)) adder_25 (.a(1'b0), .b(B24), .out(_2C_result[24]), .cin(adder_24_cout), .cout(adder_25_cout));
  Adder #(.width(1)) adder_26 (.a(1'b0), .b(B25), .out(_2C_result[25]), .cin(adder_25_cout), .cout(adder_26_cout));
  Adder #(.width(1)) adder_27 (.a(1'b0), .b(B26), .out(_2C_result[26]), .cin(adder_26_cout), .cout(adder_27_cout));
  Adder #(.width(1)) adder_28 (.a(1'b0), .b(B27), .out(_2C_result[27]), .cin(adder_27_cout), .cout(adder_28_cout));
  Adder #(.width(1)) adder_29 (.a(1'b0), .b(B28), .out(_2C_result[28]), .cin(adder_28_cout), .cout(adder_29_cout));
  Adder #(.width(1)) adder_30 (.a(1'b0), .b(B29), .out(_2C_result[29]), .cin(adder_29_cout), .cout(adder_30_cout));
  Adder #(.width(1)) adder_31 (.a(1'b0), .b(B30), .out(_2C_result[30]), .cin(adder_30_cout), .cout(adder_31_cout));
  Adder #(.width(1)) adder_32 (.a(1'b0), .b(B31), .out(_2C_result[31]), .cin(adder_31_cout));  // open: cout
endmodule

module equal_check (
  input  [31:0] A,
  input  [31:0] B,
  output result
);

  wire R0, R1, R2, R3, R4, R5, R6, R7, R8, R9, R10, R11, R12, R13, R14, R15, R16, R17, R18, R19, R20, R21,
       R22, R23, R24, R25, R26, R27, R28, R29, R30, R31;

  xnor xnor_1 (R0, A[0], B[0]);
  xnor xnor_2 (R1, A[1], B[1]);
  xnor xnor_3 (R2, A[2], B[2]);
  xnor xnor_4 (R3, A[3], B[3]);
  xnor xnor_5 (R4, A[4], B[4]);
  xnor xnor_6 (R5, A[5], B[5]);
  xnor xnor_7 (R6, A[6], B[6]);
  xnor xnor_8 (R7, A[7], B[7]);
  xnor xnor_9 (R8, A[8], B[8]);
  xnor xnor_10 (R9, A[9], B[9]);
  xnor xnor_11 (R10, A[10], B[10]);
  xnor xnor_12 (R11, A[11], B[11]);
  xnor xnor_13 (R12, A[12], B[12]);
  xnor xnor_14 (R13, A[13], B[13]);
  xnor xnor_15 (R14, A[14], B[14]);
  xnor xnor_16 (R15, A[15], B[15]);
  xnor xnor_17 (R16, A[16], B[16]);
  xnor xnor_18 (R17, A[17], B[17]);
  xnor xnor_19 (R18, A[18], B[18]);
  xnor xnor_20 (R19, A[19], B[19]);
  xnor xnor_21 (R20, A[20], B[20]);
  xnor xnor_22 (R21, A[21], B[21]);
  xnor xnor_23 (R22, A[22], B[22]);
  xnor xnor_24 (R23, A[23], B[23]);
  xnor xnor_25 (R24, A[24], B[24]);
  xnor xnor_26 (R25, A[25], B[25]);
  xnor xnor_27 (R26, A[26], B[26]);
  xnor xnor_28 (R27, A[27], B[27]);
  xnor xnor_29 (R28, A[28], B[28]);
  xnor xnor_30 (R29, A[29], B[29]);
  xnor xnor_31 (R30, A[30], B[30]);
  xnor xnor_32 (R31, A[31], B[31]);
  and and_1 (result, R0, R1, R2, R3, R4, R5, R6, R7, R8, R9, R10, R11, R12, R13, R14, R15, R16, R17, R18, R19, R20, R21, R22, R23, R24, R25, R26, R27, R28, R29, R30, R31);
endmodule
