// Logisim project regfile.circ as structural Verilog: 1 circuit, main circuit main
// Reg 0
module main (
  input  [4:0] Read_Register_1,
  input  [31:0] Reg0_is_hardcoded_to_0,
  input  [4:0] Read_Register_2,
  input  [4:0] Write_Register,
  input  [31:0] Write_Data,
  input  Write_Enable,
  input  Clock,
  output [31:0] s0_Value,
  output [31:0] s1_Value,
  output [31:0] s2_Value,
  output [31:0] ra_Value,
  output [31:0] sp_Value,
  output [31:0] Read_Data_1,
  output [31:0] Read_Data_2
);

  wire and_1_out, and_2_out, and_3_out, and_4_out, and_5_out, and_6_out, and_7_out, and_8_out, and_9_out,
       and_10_out, and_11_out, and_12_out, and_13_out, and_14_out, and_15_out, and_16_out, and_17_out,
       and_18_out, and_19_out, and_20_out, and_21_out, and_22_out, and_23_out, and_24_out, and_25_out,
       and_26_out, and_27_out, and_28_out, and_29_out, and_30_out, and_31_out, and_32_out, decoder_1_out0,
       decoder_1_out1, decoder_1_out2, decoder_1_out3, decoder_1_out4, decoder_1_out5, decoder_1_out6,
       decoder_1_out7, decoder_1_out8, decoder_1_out9, decoder_1_out10, decoder_1_out11, decoder_1_out12,
       decoder_1_out13, decoder_1_out14, decoder_1_out15, decoder_1_out16, decoder_1_out17, decoder_1_out18,
       decoder_1_out19, decoder_1_out20, decoder_1_out21, decoder_1_out22, decoder_1_out23, decoder_1_out24,
       decoder_1_out25, decoder_1_out26, decoder_1_out27, decoder_1_out28, decoder_1_out29, decoder_1_out30,
       decoder_1_out31;
  wire [31:0] Reg0_q, Reg_1_q, Reg_2_q, Reg_3_q, Reg_4_q, Reg_5_q, Reg_6_q, Reg_7_q, Reg_8_q, Reg_9_q,
       Reg_10_q, Reg_11_q, Reg_12_q, Reg_13_q, Reg_14_q, Reg_15_q, Reg_19_q, Reg_20_q, Reg_21_q, Reg_22_q,
       Reg_23_q, Reg_24_q, Reg_25_q, Reg_26_q, Reg_27_q, Reg_28_q, Reg_30_q;

  Decoder #(.select(5)) decoder_1 (
    .out0(decoder_1_out0), .out1(decoder_1_out1), .out2(decoder_1_out2), .out3(decoder_1_out3),
    .out4(decoder_1_out4), .out5(decoder_1_out5), .out6(decoder_1_out6), .out7(decoder_1_out7),
    .out8(decoder_1_out8), .out9(decoder_1_out9), .out10(decoder_1_out10), .out11(decoder_1_out11),
    .out12(decoder_1_out12), .out13(decoder_1_out13), .out14(decoder_1_out14), .out15(decoder_1_out15),
    .out16(decoder_1_out16), .out17(decoder_1_out17), .out18(decoder_1_out18), .out19(decoder_1_out19),
    .out20(decoder_1_out20), .out21(decoder_1_out21), .out22(decoder_1_out22), .out23(decoder_1_out23),
    .out24(decoder_1_out24), .out25(decoder_1_out25), .out26(decoder_1_out26), .out27(decoder_1_out27),
    .out28(decoder_1_out28), .out29(decoder_1_out29), .out30(decoder_1_out30), .out31(decoder_1_out31),
    .sel(Write_Register));  // open: en
  and and_1 (and_1_out, decoder_1_out0, Write_Enable);
  and and_2 (and_2_out, decoder_1_out1, Write_Enable);
  and and_3 (and_3_out, decoder_1_out2, Write_Enable);
  and and_4 (and_4_out, decoder_1_out3, Write_Enable);
  and and_5 (and_5_out, decoder_1_out4, Write_Enable);
  and and_6 (and_6_out, decoder_1_out5, Write_Enable);
  and and_7 (and_7_out, decoder_1_out6, Write_Enable);
  and and_8 (and_8_out, decoder_1_out7, Write_Enable);
  and and_9 (and_9_out, decoder_1_out8, Write_Enable);
  and and_10 (and_10_out, decoder_1_out9, Write_Enable);
  and and_11 (and_11_out, decoder_1_out10, Write_Enable);
  and and_12 (and_12_out, decoder_1_out11, Write_Enable);
  and and_13 (and_13_out, decoder_1_out12, Write_Enable);
  and and_14 (and_14_out, decoder_1_out13, Write_Enable);
  and and_15 (and_15_out, decoder_1_out14, Write_Enable);
  and and_16 (and_16_out, decoder_1_out15, Write_Enable);
  and and_17 (and_17_out, decoder_1_out16, Write_Enable);
  and and_18 (and_18_out, decoder_1_out17, Write_Enable);
  and and_19 (and_19_out, decoder_1_out18, Write_Enable);
  and and_20 (and_20_out, decoder_1_out19, Write_Enable);
  and and_21 (and_21_out, decoder_1_out20, Write_Enable);
  and and_22 (and_22_out, decoder_1_out21, Write_Enable);
  and and_23 (and_23_out, decoder_1_out22, Write_Enable);
  and and_24 (and_24_out, decoder_1_out23, Write_Enable);
  and and_25 (and_25_out, decoder_1_out24, Write_Enable);
  and and_26 (and_26_out, decoder_1_out25, Write_Enable);
  and and_27 (and_27_out, decoder_1_out26, Write_Enable);
  and and_28 (and_28_out, decoder_1_out27, Write_Enable);
  and and_29 (and_29_out, decoder_1_out28, Write_Enable);
  and and_30 (and_30_out, decoder_1_out29, Write_Enable);
  and and_31 (and_31_out, decoder_1_out30, Write_Enable);
  and and_32 (and_32_out, decoder_1_out31, Write_Enable);
  Register #(.width(32)) Reg0 (.D(Reg0_is_hardcoded_to_0), .en(and_1_out), .Q(Reg0_q), .clk(Clock));  // open: clr
  Register #(.width(32)) Reg_1 (.D(Write_Data), .en(and_2_out), .Q(Reg_1_q), .clk(Clock));  // open: clr
  Register #(.width(32)) Reg_2 (.D(Write_Data), .en(and_3_out), .Q(Reg_2_q), .clk(Clock));  // open: clr
  Register #(.width(32)) Reg_3 (.D(Write_Data), .en(and_4_out), .Q(Reg_3_q), .clk(Clock));  // open: clr
  Register #(.width(32)) Reg_4 (.D(Write_Data), .en(and_5_out), .Q(Reg_4_q), .clk(Clock));  // open: clr
  Register #(.width(32)) Reg_5 (.D(Write_Data), .en(and_6_out), .Q(Reg_5_q), .clk(Clock));  // open: clr
  Register #(.width(32)) Reg_6 (.D(Write_Data), .en(and_7_out), .Q(Reg_6_q), .clk(Clock));  // open: clr
  Register #(.width(32)) Reg_7 (.D(Write_Data), .en(and_8_out), .Q(Reg_7_q), .clk(Clock));  // open: clr
  Register #(.width(32)) Reg_8 (.D(Write_Data), .en(and_9_out), .Q(Reg_8_q), .clk(Clock));  // open: clr
  Register #(.width(32)) Reg_9 (.D(Write_Data), .en(and_10_out), .Q(Reg_9_q), .clk(Clock));  // open: clr
  Register #(.width(32)) Reg_10 (.D(Write_Data), .en(and_11_out), .Q(Reg_10_q), .clk(Clock));  // open: clr
  Register #(.width(32)) Reg_11 (.D(Write_Data), .en(and_12_out), .Q(Reg_11_q), .clk(Clock));  // open: clr
  Register #(.width(32)) Reg_12 (.D(Write_Data), .en(and_13_out), .Q(Reg_12_q), .clk(Clock));  // open: clr
  Register #(.width(32)) Reg_13 (.D(Write_Data), .en(and_14_out), .Q(Reg_13_q), .clk(Clock));  // open: clr
  Register #(.width(32)) Reg_14 (.D(Write_Data), .en(and_15_out), .Q(Reg_14_q), .clk(Clock));  // open: clr
  Register #(.width(32)) Reg_15 (.D(Write_Data), .en(and_16_out), .Q(Reg_15_q), .clk(Clock));  // open: clr
  Register #(.width(32)) Reg_16 (.D(Write_Data), .en(and_17_out), .Q(s0_Value), .clk(Clock));  // open: clr
  Register #(.width(32)) Reg_17 (.D(Write_Data), .en(and_18_out), .Q(s1_Value), .clk(Clock));  // open: clr
  Register #(.width(32)) Reg_18 (.D(Write_Data), .en(and_19_out), .Q(s2_Value), .clk(Clock));  // open: clr
  Register #(.width(32)) Reg_19 (.D(Write_Data), .en(and_20_out), .Q(Reg_19_q), .clk(Clock));  // open: clr
  Register #(.width(32)) Reg_20 (.D(Write_Data), .en(and_21_out), .Q(Reg_20_q), .clk(Clock));  // open: clr
  Register #(.width(32)) Reg_21 (.D(Write_Data), .en(and_22_out), .Q(Reg_21_q), .clk(Clock));  // open: clr
  Register #(.width(32)) Reg_22 (.D(Write_Data), .en(and_23_out), .Q(Reg_22_q), .clk(Clock));  // open: clr
  Register #(.width(32)) Reg_23 (.D(Write_Data), .en(and_24_out), .Q(Reg_23_q), .clk(Clock));  // open: clr
  Register #(.width(32)) Reg_24 (.D(Write_Data), .en(and_25_out), .Q(Reg_24_q), .clk(Clock));  // open: clr
  Register #(.width(32)) Reg_25 (.D(Write_Data), .en(and_26_out), .Q(Reg_25_q), .clk(Clock));  // open: clr
  Register #(.width(32)) Reg_26 (.D(Write_Data), .en(and_27_out), .Q(Reg_26_q), .clk(Clock));  // open: clr
  Register #(.width(32)) Reg_27 (.D(Write_Data), .en(and_28_out), .Q(Reg_27_q), .clk(Clock));  // open: clr
  Register #(.width(32)) Reg_28 (.D(Write_Data), .en(and_29_out), .Q(Reg_28_q), .clk(Clock));  // open: clr
  Register #(.width(32)) Reg_29 (.D(Write_Data), .en(and_30_out), .Q(sp_Value), .clk(Clock));  // open: clr
  Register #(.width(32)) Reg_30 (.D(Write_Data), .en(and_31_out), .Q(Reg_30_q), .clk(Clock));  // open: clr
  Register #(.width(32)) Reg_31 (.D(Write_Data), .en(and_32_out), .Q(ra_Value), .clk(Clock));  // open: clr
  Multiplexer #(.select(5), .width(32)) multiplexer_1 (
    .in0(Reg0_q), .in1(Reg_1_q), .in2(Reg_2_q), .in3(Reg_3_q), .in4(Reg_4_q), .in5(Reg_5_q), .in6(Reg_6_q),
    .in7(Reg_7_q), .in8(Reg_8_q), .in9(Reg_9_q), .in10(Reg_10_q), .in11(Reg_11_q), .in12(Reg_12_q),
    .in13(Reg_13_q), .in14(Reg_14_q), .in15(Reg_15_q), .in16(s0_Value), .in17(s1_Value), .in18(s2_Value),
    .in19(Reg_19_q), .in20(Reg_20_q), .in21(Reg_21_q), .in22(Reg_22_q), .in23(Reg_23_q), .in24(Reg_24_q),
    .in25(Reg_25_q), .in26(Reg_26_q), .in27(Reg_27_q), .in28(Reg_28_q), .in29(sp_Value), .in30(Reg_30_q),
    .in31(ra_Value), .out(Read_Data_1), .sel(Read_Register_1));  // open: en
  Multiplexer #(.select(5), .width(32)) multiplexer_2 (
    .in0(Reg0_q), .in1(Reg_1_q), .in2(Reg_2_q), .in3(Reg_3_q), .in4(Reg_4_q), .in5(Reg_5_q), .in6(Reg_6_q),
    .in7(Reg_7_q), .in8(Reg_8_q), .in9(Reg_9_q), .in10(Reg_10_q), .in11(Reg_11_q), .in12(Reg_12_q),
    .in13(Reg_13_q), .in14(Reg_14_q), .in15(Reg_15_q), .in16(s0_Value), .in17(s1_Value), .in18(s2_Value),
    .in19(Reg_19_q), .in20(Reg_20_q), .in21(Reg_21_q), .in22(Reg_22_q), .in23(Reg_23_q), .in24(Reg_24_q),
    .in25(Reg_25_q), .in26(Reg_26_q), .in27(Reg_27_q), .in28(Reg_28_q), .in29(sp_Value), .in30(Reg_30_q),
    .in31(ra_Value), .out(Read_Data_2), .sel(Read_Register_2));  // open: en

  // Other names for the same wires on the sheet: clk = Clock; ra[31:0] = ra_Value; read_data1[31:0] = Read_Data_1;
  //   read_data2[31:0] = Read_Data_2; read_reg1[4:0] = Read_Register_1; read_reg2[4:0] = Read_Register_2;
  //   s0[31:0] = s0_Value; s1[31:0] = s1_Value; s2[31:0] = s2_Value; sp[31:0] = sp_Value; write_en = Write_Enable;
  //   write_reg[4:0] = Write_Register

  // Notes on the sheet:
  //   of the registers will allow
  //   INPUTS to your circuit
  //   Connecting the write_register
  //   to the decoder and connecting             
  //   its output to the load input
  //   it to choose which of these
  //   32 registers to write to
  //   DON'T CHANGE THE LOCATIONS OF THE INPUTS AND OUTPUTS!
  //   And gate allow the loading of the
  //   register when the write enable 
  //   is set to 1
  //   These are DEBUG/TEST outputs from your circuit.
  //   WriteData is connected
  //   to the register so that
  //   it can be stored on
  //      the raising edge of the clock
  //   OUTPUTS from your circuit
  //   Having two read_date outputs require
  //   two multiplexer so that Register 1 and
  //   Register 2 know which register to transfer
  //      its information to one of the read_data output
endmodule
