// Logisim project regfile-allRegsWriteRead.circ as structural Verilog: 1 circuit, main circuit main
module main (
  output [7:0] test_num,
  output [31:0] Reg_0_Value,
  output [31:0] Reg_1_Value,
  output [31:0] Reg_2_Value,
  output [31:0] Reg_3_Value,
  output [31:0] Reg_4_Value,
  output [31:0] Read_Data_1,
  output [31:0] Read_Data_2
);

  wire clock_1_out;
  wire [7:0] adder_1_out;
  wire [15:0] rom_2_data;
  wire [31:0] WriteData;

  Register register_1 (.D(adder_1_out), .en(1'b1), .Q(test_num), .clk(clock_1_out));  // open: clr
  Adder adder_1 (.a(8'h1), .b(test_num), .out(adder_1_out));  // open: cin, cout
  ROM #(.dataWidth(32)) rom_1 (.addr(test_num), .data(WriteData));  // open: sel
  ROM #(.dataWidth(16)) rom_2 (.addr(test_num), .data(rom_2_data), .sel(1'b1));
  Clock clock_1 (.out(clock_1_out));
  regfile_main main_1 (
    .Read_Register_1(rom_2_data[4:0]), .Read_Register_2(rom_2_data[9:5]), .Write_Register(rom_2_data[14:10]),
    .Write_Data(WriteData), .Write_Enable(rom_2_data[15]), .Clock(clock_1_out), .Read_Data_1(Read_Data_1),
    .Read_Data_2(Read_Data_2), .s0_Value(Reg_0_Value), .s1_Value(Reg_1_Value), .s2_Value(Reg_2_Value),
    .ra_Value(Reg_3_Value), .sp_Value(Reg_4_Value));  // open: Reg0_is_hardcoded_to_0

  // Notes on the sheet:
  //   contents of rom_1 (hex, n*v repeats v):
  //   1 2 3 4 5 6 7 8 9 a b c d e f 10 11 12 13 14 15 16 17 18 19 1a 1b 1c 1d 1e 1f 20
  //   contents of rom_2 (hex, n*v repeats v):
  //   8400 8820 8c40 9060 9480 98a0 9cc0 90e0 9480 a8a0 ad40 b160 b580 b9a0 bdc0 c1e0 c600 ca20 ce40 d260
  //   d680 daa0 dec0 e2e0 e700 eb20 ef40 f360 f780 fba0 ffc0 3e0
  //   YOUR REGFILE SHOULD FIT IN HERE!
  //   There should be no blue/red wires here, and the result shouldn't be x's.
endmodule
